# Fritzing sketch Bubbler Electronics (saved by Fritzing 0.9.1b)
circuit board: 8.46667cm x 5.64444cm
breadboards: 1

parts:
  Part1 = Arduino Uno (Rev3)
  M1 = DC Motor
  Q1 = TRANSISTOR_NPN [package=to-92-ammo]
  R1 = Resistor [tolerance=±5% resistance=220 package=THT]
  D1 = Rectifier Diode [part_number=1N4001 package="300 mil [THT]"]
  IC1 = IC, DIP package, 8 pins [chip_label=IC]  # not connected

nets:
  N1: Part1.D3_PWM, R1.Pin_0
  N2: Part1.5V, M1.pin_1, D1.cathode
  N3: Part1.GND, Q1.E
  N4: M1.pin_2, Q1.C, D1.anode
  N5: Q1.B, R1.Pin_1

// code stored in the sketch: Bubbler.ino
int motorPin = 3;
int LED = 13;

void motorOnThenOff() {
	int onTime = 4000;  // milliseconds
	int offTime = 2000; // milliseconds
	digitalWrite(motorPin, HIGH);
	digitalWrite(LED, HIGH);
	delay(onTime);
	digitalWrite(motorPin, LOW);
	digitalWrite(LED, LOW);
	delay(offTime);
	}

void motorOnThenOffWithSpeed() {
	int onSpeed = 200;
	int onTime = 3000;
	int offSpeed = 50;
	int offTime = 1000;

	analogWrite(motorPin, onSpeed);
	digitalWrite(LED, HIGH);
	delay(onTime);
	analogWrite(motorPin, offSpeed);
	digitalWrite(LED, LOW);
	delay(offTime);
	}

void motorAcceleration() {
	int delayTime = 50;
	for(int i=0; i < 256; i++) {
		analogWrite(motorPin, i);
		delay(delayTime);
		}
	for(int i=255; i >=0; i--) {
		analogWrite(motorPin, i);
		delay(delayTime);
		}
	}

void setup_pins() {
	// Now configure the pins we're actually using
	pinMode(motorPin, OUTPUT);
	pinMode(LED, OUTPUT);
	}

void setup() {
	// put your setup code here, to run once:
	setup_pins();
}

void loop() {
	// put your main code here, to run repeatedly:
	motorOnThenOff();
	//motorOnThenOffWithSpeed();
	//motorAcceleration();
}
